# Fritzing sketch arduino_on (saved by Fritzing 0.9.1b)
breadboards: 1

parts:
  Part1 = Arduino Uno (Rev3)
  LED1 = LED - 5mm [color="Red (633nm)" package="5 mm [THT]"]
  R1 = Resistor [tolerance=±5% resistance=10k package=THT]

nets:
  N1: Part1.D3_PWM, R1.Pin_1
  N2: Part1.GND, LED1.cathode
  N3: LED1.anode, R1.Pin_0

notes:
  Red wire is connected to Pin 3 and the resistor. Black wire is connected to GND and the negative(short) leg of the LED.

// code stored in the sketch: led_basicOnOff.ino
//this is a comment, it does not affect code
//these are meant for people to read
//you need to leave notes that tell other people what your code is actually doing

//the setup function sets the modes of the pins we are using
//it only runs once
void setup(){
	pinMode(3, OUTPUT);//set pin 3 as an output
}//end setup

//the loop function runs after the setup function
//the loop function will run the code inside of the braces so long as the Arduino is on!
void loop(){
	digitalWrite(3, HIGH);//use pin 3, send it a command to tell it to turn on, HIGH means on
	delay(1000);//delay the program for 1000 milli-seconds, meaning wait for 1 second
	digitalWrite(3, LOW);//use pin 3, send it a command to tell it to turn off, LOW means off
	delay(1000);//delay the program for 1000 milli-seconds, meaning wait for 1 second
}
