# Fritzing sketch led_on (saved by Fritzing 0.9.1b)
breadboards: 1

parts:
  BAT1 = Battery Holders [package=battery-aa-kit]
  BAT2 = Battery Holders [package=battery-aa-kit]
  BAT3 = Battery Holders [package=battery-aa-kit]
  R1 = Resistor [tolerance=±5% resistance=1k package=THT]
  LED1 = LED - 5mm [color="Red (633nm)" package="5 mm [THT]"]

nets:
  N1: BAT1.+, LED1.cathode
  N2: BAT1.-, BAT2.+
  N3: BAT2.-, BAT3.+
  N4: BAT3.-, R1.Pin_1
  N5: R1.Pin_0, LED1.anode

notes:
  Hook up a battery that is at least 3 volts. In this example, there are three AA batteries connected in series to add up to 4.5 volts.
  The resistor is connected to the LED's positive(long) leg and the positive of the batteries. The LED's negative(short) leg is connected to the negative of the batteries.
  *Normally, you would draw all three 1.5 volt batteries as a single 4.5 battery symbol.*
