# Fritzing sketch 555_photoresistor_theremin (saved by Fritzing 0.9.1b)
breadboards: 1

parts:
  U1 = 555 Timer [package="DIP8 [THT]"]
  C1 = Ceramic Capacitor [capacitance=0.1µF package="100 mil [THT, multilayer]"]
  C2 = Ceramic Capacitor [capacitance=0.1µF package="100 mil [THT, multilayer]"]
  R1 = Resistor [tolerance=±5% resistance=10k package=THT]
  R2 = Resistor [tolerance=±5% resistance=1M package=THT]
  C3 = Electrolytic Capacitor [capacitance=1µF package="100 mil [THT, electrolytic]"]
  R3 = Photocell (LDR) [package=THT]
  J1 = Piezo Speaker

nets:
  N1: U1.Ground, U1.Reset, C1.0, C2.0, R2.Pin_1, J1.pin1
  N2: U1.Trigger, U1.Threshold, C1.1, C2.1, R2.Pin_0, R3.pin_0
  N3: U1.Output, C3.+
  N4: U1.Discharge, R1.Pin_0, R3.pin_1
  N5: U1.Vcc_Supply_Voltage, R1.Pin_1
  N6: C3.-, J1.pin2

notes:
  there are two capacitors here!
